// Logisim project main.circ as structural Verilog: 6 circuits, main circuit main
module UP (
);

  wire button_1_out, button_2_out, button_3_out, button_4_out, main_1_led_pause, main_1_led_pwr;
  wire [8:0] trm;

  TTY #(.cols(80), .rows(25)) tty_1 (.data(trm[6:0]), .clk(trm[7]), .clr(trm[8]));  // open: we
  Button button_1 (.out(button_1_out));
  Button button_2 (.out(button_2_out));
  Button button_3 (.out(button_3_out));
  Button button_4 (.out(button_4_out));
  LED led_1 (.in(main_1_led_pwr));
  main main_1 (
    .PAUSE_CONT(button_2_out), .RESET(button_3_out), .PULSE(button_4_out), .ON_OFF(button_1_out),
    .LED_PWR(main_1_led_pwr), .LED_PAUSE(main_1_led_pause), .TRM_ASCII(trm[6:0]), .TRM_CLK(trm[7]),
    .TRM_RST(trm[8]));
  LED led_2 (.in(main_1_led_pause));
endmodule

module main (
  input  ON_OFF,
  input  PAUSE_CONT,
  input  RESET,
  input  PULSE,
  output LED_PWR,
  output LED_PAUSE,
  output [6:0] TRM_ASCII,
  output TRM_CLK,
  output TRM_RST
);

  wire and_1_out, and_2_out, and_3_out, and_4_out, and_5_out, and_6_out, button_1_out, button_2_out,
       button_3_out, button_4_out, button_5_out, CLK, IO_EN, IRQ, or_1_out, or_2_out, or_3_out, or_4_out,
       RAM0_EN, RAM1_EN, ROM0_EN, RST, RWB;
  wire [7:0] D, ROM0_data;
  wire [15:0] A;

  TTY #(.rows(16)) tty_1 (.data(TRM_ASCII), .clk(TRM_CLK), .clr(TRM_RST));  // open: we
  or or_1 (or_1_out, ON_OFF, button_1_out);
  Button button_1 (.out(button_1_out));
  or or_2 (or_2_out, PAUSE_CONT, button_2_out);
  Button button_2 (.out(button_2_out));
  or or_3 (or_3_out, RESET, button_3_out);
  Button button_3 (.out(button_3_out));
  or or_4 (or_4_out, PULSE, button_4_out);
  Button button_4 (.out(button_4_out));
  Button button_5 (.out(button_5_out));
  clk_ctrl clk_ctrl_1 (
    .PAUSE_CONT(or_2_out), .ON_OFF(or_1_out), .RESET(or_3_out), .PULSE(or_4_out), .pause(LED_PAUSE),
    .power(LED_PWR), .CLK(CLK), .RST(RST));
  PIC pic_1 (
    .IR0(button_5_out), .RST(RST), .A(A), .RWB(RWB), .IO_EN(IO_EN), .IRQ(IRQ), .D(D));  // open: IR6, IR5, IR4, IR3, IR7, IR2, IR1
  LED led_1 (.in(LED_PWR));
  LED led_2 (.in(LED_PAUSE));
  and and_1 (and_1_out, LED_PWR, ~LED_PAUSE);  // AND_Gate
  Pull_Resistor #(.pull(1)) pull_resistor_1 ();  // open: node
  // W65C02S__Expert w65c02s_expert_1: pin names not known; wires that end beside it: and_1_out, IRQ, CLK, RWB, D, A
  terminal_ctrl terminal_ctrl_1 (
    .A(A), .IO_EN(IO_EN), .CLK(CLK), .RST(RST), .RWB(RWB), .Di(D), .Do(D), .TRM_ASCII(TRM_ASCII),
    .TRM_RST(TRM_RST), .TRM_CLK(TRM_CLK));
  // NOT_Gate not_1 has open pins: in=RST, out=open
  Pull_Resistor #(.pull(1)) pull_resistor_2 ();  // open: node
  Pull_Resistor #(.pull(1)) pull_resistor_3 ();  // open: node
  // Probe on D
  // Probe on A
  PLA #(.in_width(16), .out_width(4), .\table ("0xxxxxxxxxxxxxxx 0001 # RAM0\n10xxxxxxxxxxxxxx 0010 # RAM1\n1100xxxxxxxxxxxx 0010 # RAM1\n1101xxxxxxxxxxxx 0100 # IO\n111xxxxxxxxxxxxx 1000 # ROM")) pla_1 (
    .in(A), .out({ROM0_EN, IO_EN, RAM1_EN, RAM0_EN}));
  and and_2 (and_2_out, ~RWB, RAM0_EN);  // AND_Gate
  and and_3 (and_3_out, RAM0_EN, RWB);
  and and_4 (and_4_out, ~RWB, RAM1_EN);  // AND_Gate
  and and_5 (and_5_out, RAM1_EN, RWB);
  RAM #(.addrWidth(15), .clearpin("true"), .databus("bidir")) RAM0 (
    .addr(A[14:0]), .we(and_2_out), .oe(and_3_out), .clk(CLK), .data(D), .clr(RST));
  RAM #(.addrWidth(15), .clearpin("true"), .databus("bidir")) RAM1 (
    .addr(A[14:0]), .we(and_4_out), .oe(and_5_out), .clk(CLK), .data(D), .clr(RST));
  ROM #(.addrWidth(13)) ROM0 (.addr(A[12:0]), .data(ROM0_data));
  and and_6 (and_6_out, ROM0_EN, RWB);
  assign D = and_6_out ? ROM0_data : 8'bz;  // Controlled_Buffer controlled_buffer_1

  // Notes on the sheet:
  //   contents of ROM0 (hex, n*v repeats v):
  //   38 a5 20 e9 4 85 20 b0 2 c6 21 a5 1 a0 1 91 20 a5 0 88 91 20 c8 b1 20 a0 3 91 20 a0 0 b1 20 a0 2 91
  //   20 80 10 a0 0 b1 20 18 69 1 91 20 c8 b1 20 69 0 91 20 a0 0 b1 20 85 e c8 b1 20 85 f b2 e d0 e1 a0 0
  //   b1 20 38 a0 2 f1 20 48 88 b1 20 a0 3 f1 20 aa 68 85 1f 18 a5 20 69 4 85 20 90 2 e6 21 a5 1f 60 38 a5
  //   20 e9 19 85 20 b0 2 c6 21 a5 1 a0 5 91 20 a5 0 88 91 20 a5 25 88 91 20 a5 24 88 91 20 a5 23 88 91 20
  //   a5 22 88 91 20 a5 20 18 69 6 85 e a5 21 69 0 85 f a0 10 b9 a e8 91 e 88 10 f8 a9 0 a0 18 91 20 a9 9
  //   88 91 20 a0 4 b1 20 18 a0 17 71 20 85 0 a0 5 b1 20 a0 18 71 20 85 1 a9 0 92 0 80 71 a5 20 18 69 6 85
  //   0 a5 21 69 0 85 1 a0 0 b1 20 29 f 85 1f a0 4 b1 20 18 a0 17 71 20 85 2 a0 5 b1 20 a0 18 71 20 85 3
  //   a5 1f a8 b1 0 92 2 a0 3 b1 20 85 1e 88 b1 20 85 1f 88 b1 20 85 1d 88 b1 20 46 1e 66 1f 66 1d 6a 46
  //   1e 66 1f 66 1d 6a 46 1e 66 1f 66 1d 6a 46 1e 66 1f 66 1d 6a 91 20 a5 1d c8 91 20 a5 1f c8 91 20 a5
  //   1e c8 91 20 a0 17 b1 20 38 e9 1 91 20 c8 b1 20 e9 0 91 20 88 b1 20 c8 11 20 f0 3 4c d0 e0 a0 4 b1 20
  //   85 e c8 b1 20 85 f a9 20 92 e 18 a5 20 69 19 85 20 90 2 e6 21 60 38 a5 20 e9 e 85 20 b0 2 c6 21 a5 1
  //   a0 1 91 20 a5 0 88 91 20 c8 b1 20 85 1 88 b1 20 85 0 20 f4 e7 a0 0 b1 20 18 69 10 85 0 c8 b1 20 69 0
  //   85 1 a5 0 a0 3 91 20 a5 1 88 91 20 20 f4 e7 a0 2 b1 20 85 1 c8 b1 20 85 0 a0 0 b1 20 18 69 10 85 0
  //   c8 b1 20 69 0 85 1 a5 0 a0 3 91 20 a5 1 88 91 20 20 0 e0 85 1f a0 2 b1 20 85 1 a5 1f c8 b1 20 85 0
  //   a5 1f c8 91 20 8a c8 91 20 a0 1 b1 20 a0 7 91 20 a0 0 b1 20 a0 6 91 20 a0 0 b1 20 18 69 10 85 0 c8
  //   b1 20 69 0 85 1 a5 0 18 a0 4 71 20 85 0 a5 1 c8 71 20 85 1 a5 0 85 22 a5 1 85 23 a2 0 c9 0 10 1 ca
  //   86 24 86 25 a5 22 29 f0 85 22 a9 0 85 24 85 25 a5 23 85 1 a5 22 85 0 18 69 10 a0 8 91 20 a5 1 69 0
  //   c8 91 20 a0 8 b1 20 85 e c8 b1 20 85 f a9 0 85 22 85 23 85 24 a0 3 b1 e 85 25 a0 0 84 25 84 24 84 23
  //   85 22 a0 8 b1 20 85 e c8 b1 20 85 f a9 0 85 26 85 27 a0 2 b1 e 85 28 a9 0 85 29 a5 27 a4 28 84 27 a4
  //   29 84 28 a0 0 84 29 85 26 a5 22 5 26 85 22 a5 23 5 27 85 23 a5 24 5 28 85 24 a5 25 5 29 85 25 a0 8
  //   b1 20 85 e c8 b1 20 85 f a9 0 85 26 a0 1 b1 e 85 27 a9 0 85 28 85 29 a5 28 85 29 a5 27 85 28 a5 26
  //   85 27 a9 0 85 26 a5 22 5 26 85 22 a5 23 5 27 85 23 a5 24 5 28 85 24 a5 25 5 29 85 25 a0 8 b1 20 85 e
  //   c8 b1 20 85 f b2 e 85 26 a9 0 85 27 85 28 85 29 a5 26 85 29 a9 0 85 27 85 28 85 26 a5 22 5 26 85 22
  //   a5 23 5 27 85 23 a5 24 5 28 85 24 a5 25 5 29 85 25 a5 22 29 f0 c8 91 20 a5 23 c8 91 20 a9 0 c8 91 20
  //   c8 91 20 a0 8 b1 20 18 69 10 85 0 c8 b1 20 69 0 85 1 a5 0 a0 3 91 20 a5 1 88 91 20 20 f4 e7 a0 2 b1
  //   20 85 1 c8 b1 20 85 0 a0 a b1 20 c8 11 20 c8 11 20 c8 11 20 d0 2 80 20 a0 b b1 20 85 1 88 b1 20 85 0
  //   18 a0 6 71 20 a0 8 91 20 a5 1 88 71 20 a0 9 91 20 4c 5e e2 18 a5 20 69 e 85 20 90 2 e6 21 60 4*0 40
  //   40 a2 ff 9a e8 a9 0 85 20 a9 d0 85 21 58 a9 f0 85 0 a9 e3 85 1 20 77 e1 78 db cb 80 fd 17*0 2d 72 6f
  //   6d 31 66 73 2d 0 0 1 d0 3f 15 b5 7a 54 45 53 54 5f 56 4f 4c 55 4d 45 8*0 49 0 0 0 20 4*0 d1 ff ff 97
  //   2e 18*0 60 0 0 0 20 4*0 d1 d1 ff 80 2e 2e 16*0 1 9 0 0 0 80 4*0 2d 2c 27 a0 73 6f 6d 65 5f 64 69 72
  //   11*0 c2 7*0 18 b3 69 21 3c 74 68 69 72 64 2e 74 78 74 7*0 74 68 69 72 64 20 66 69 6c 65 20 69 6e 20
  //   64 69 72 65 63 74 6f 72 79 a 11*0 e0 0 0 0 20 4*0 d1 d1 ff 0 2e 2e 21*0 60 4*0 d1 ff ff a0 2e 17*0 1
  //   3a 7*0 e b6 36 6c d6 73 65 63 6f 6e 64 2e 73 68 7*0 65 63 68 6f 20 32 6e 64 20 66 69 6c 65 a 4*0 1
  //   50 0 0 1 5*0 29 35 91 47 68 5f 6c 69 6e 6b 12*0 1 83 7*0 9 20 1d 22 aa 73 79 6d 5f 6c 69 6e 6b 8*0
  //   73 65 63 6f 6e 64 2e 73 68 10*0 2 7*0 2f b1 68 18 e4 66 69 72 73 74 2e 74 78 74 7*0 74 68 69 73 20
  //   69 73 20 61 20 66 69 72 73 74 20 66 69 6c 65 2e a 73 6f 6d 65 20 74 65 78 74 20 66 6f 72 20 66 69 6c
  //   6c 69 6e 67 20 69 74 a 561*0 8d 10 d0 60 48 5a a0 ff c8 b1 0 f0 5 8d 10 d0 80 f6 a9 a 8d 10 d0 7a 68
  //   60 30 31 32 33 34 35 36 37 38 39 41 42 43 44 45 46 6112*0 c0 e3 c2 e3 c1 e3
endmodule

module clk_ctrl (
  input  PAUSE_CONT,
  input  ON_OFF,
  input  RESET,
  input  PULSE,
  output pause,
  output power,
  output CLK,
  output RST
);

  wire clock_1_out, controlled_buffer_1_out, d_ff_1_q, or_1_out, or_2_out, t_ff_1_qn, t_ff_2_qn;

  T_Flip_Flop t_ff_1 (.T(PAUSE_CONT), .clk(PAUSE_CONT), .Q(pause), .Qn(t_ff_1_qn), .reset(or_2_out));  // open: preset
  T_Flip_Flop t_ff_2 (.T(ON_OFF), .clk(ON_OFF), .Q(power), .Qn(t_ff_2_qn));  // open: reset, preset
  Clock clock_1 (.out(clock_1_out));
  or or_1 (or_1_out, clock_1_out, PULSE);
  assign controlled_buffer_1_out = t_ff_1_qn ? or_1_out : 1'bz;  // Controlled_Buffer controlled_buffer_1
  or or_2 (or_2_out, t_ff_2_qn, RESET);
  D_Flip_Flop d_ff_1 (
    .D(power), .clk(controlled_buffer_1_out), .Q(d_ff_1_q), .Qn(RST), .reset(or_2_out));  // open: preset
  Pull_Resistor pull_resistor_1 (.node(controlled_buffer_1_out));
  and and_1 (CLK, controlled_buffer_1_out, d_ff_1_q);
endmodule

module PIC (
  input  IR7,
  input  IR6,
  input  RST,
  input  IR5,
  input  [15:0] A,
  input  RWB,
  input  IO_EN,
  input  IR4,
  input  IR3,
  input  IR2,
  input  IR1,
  input  IR0,
  output [7:0] D,
  output IRQ
);

  wire and_1_out, comparator_1_eq, d_ff_1_q, d_ff_2_q, d_ff_3_q, d_ff_4_q, d_ff_5_q, d_ff_6_q, d_ff_7_q,
       d_ff_8_q, decoder_1_out0, decoder_1_out1, decoder_1_out2, decoder_1_out3, decoder_1_out4,
       decoder_1_out5, decoder_1_out6, decoder_1_out7, not_2_out, or_1_out, or_2_out, or_3_out, or_4_out,
       or_5_out, or_6_out, or_7_out, or_8_out, priority_encoder_1_gs, sel;
  wire [2:0] not_1_out, priority_encoder_1_out, register_1_q;
  wire [7:0] INT_CODE_out;

  D_Flip_Flop d_ff_1 (.D(1'b1), .clk(IR7), .Q(d_ff_1_q), .reset(or_1_out));  // open: Qn, preset
  or or_1 (or_1_out, RST, decoder_1_out7);
  D_Flip_Flop d_ff_2 (.D(1'b1), .clk(IR6), .Q(d_ff_2_q), .reset(or_2_out));  // open: Qn, preset
  or or_2 (or_2_out, RST, decoder_1_out6);
  D_Flip_Flop d_ff_3 (.D(1'b1), .clk(IR5), .Q(d_ff_3_q), .reset(or_3_out));  // open: Qn, preset
  or or_3 (or_3_out, RST, decoder_1_out5);
  D_Flip_Flop d_ff_4 (.D(1'b1), .clk(IR4), .Q(d_ff_4_q), .reset(or_4_out));  // open: Qn, preset
  or or_4 (or_4_out, RST, decoder_1_out4);
  D_Flip_Flop d_ff_5 (.D(1'b1), .clk(IR3), .Q(d_ff_5_q), .reset(or_5_out));  // open: Qn, preset
  or or_5 (or_5_out, RST, decoder_1_out3);
  D_Flip_Flop d_ff_6 (.D(1'b1), .clk(IR2), .Q(d_ff_6_q), .reset(or_6_out));  // open: Qn, preset
  or or_6 (or_6_out, RST, decoder_1_out2);
  D_Flip_Flop d_ff_7 (.D(1'b1), .clk(IR1), .Q(d_ff_7_q), .reset(or_7_out));  // open: Qn, preset
  or or_7 (or_7_out, RST, decoder_1_out1);
  D_Flip_Flop d_ff_8 (.D(1'b1), .clk(IR0), .Q(d_ff_8_q), .reset(or_8_out));  // open: Qn, preset
  or or_8 (or_8_out, RST, decoder_1_out0);
  Decoder #(.select(3)) decoder_1 (
    .out0(decoder_1_out0), .out1(decoder_1_out1), .out2(decoder_1_out2), .out3(decoder_1_out3),
    .out4(decoder_1_out4), .out5(decoder_1_out5), .out6(decoder_1_out6), .out7(decoder_1_out7),
    .sel(register_1_q), .en(and_1_out));
  Register #(.trigger("high"), .width(3)) register_1 (
    .D(not_1_out), .en(priority_encoder_1_gs), .clk(not_2_out), .Q(register_1_q), .clr(RST));
  assign not_1_out = ~priority_encoder_1_out;  // NOT_Gate not_1, 3 bits wide
  Priority_Encoder priority_encoder_1 (
    .in0(d_ff_1_q), .in1(d_ff_2_q), .in2(d_ff_3_q), .in3(d_ff_4_q), .in4(d_ff_5_q), .in5(d_ff_6_q),
    .in6(d_ff_7_q), .in7(d_ff_8_q), .out(priority_encoder_1_out), .gs(priority_encoder_1_gs));  // open: en_in, en_out
  not not_2 (not_2_out, and_1_out);
  and and_1 (and_1_out, priority_encoder_1_gs, sel);
  PLA #(.in_width(3), .out_width(8), .\table ("000 00000000 # IRQ0\n001 00000000 # IRQ1\n010 00000000 # IRQ2\n011 00000000 # IRQ3\n100 00000000 # IRQ4\n101 00000000 # IRQ5\n110 00000000 # IRQ6\n111 00000000 # IRQ7")) INT_CODE (
    .in(register_1_q), .out(INT_CODE_out));
  assign D = sel ? INT_CODE_out : 8'bz;  // Controlled_Buffer controlled_buffer_1
  not not_3 (IRQ, priority_encoder_1_gs);
  Comparator #(.mode("unsigned")) comparator_1 (.a(A[11:4]), .b({8{1'b0}}), .eq(comparator_1_eq));  // open: gt, lt
  and and_2 (sel, comparator_1_eq, RWB, IO_EN);

  // Notes on the sheet:
  //   IR6: pull=down
  //   IR5: pull=down
  //   IR4: pull=down
  //   IR3: pull=down
  //   IR7: pull=down
  //   IR2: pull=down
  //   IR1: pull=down
  //   IR0: pull=down
endmodule

module terminal_ctrl (
  input  [15:0] A,
  input  [7:0] Di,
  input  IO_EN,
  input  CLK,
  input  RST,
  input  RWB,
  output [6:0] TRM_ASCII,
  output TRM_RST,
  output TRM_CLK,
  output [7:0] Do
);

  wire and_1_out, and_3_out, and_4_out, comparator_1_eq, sel;

  assign Do = and_1_out ? {8{1'b0}} : 8'bz;  // Controlled_Buffer controlled_buffer_1
  Comparator #(.mode("unsigned")) comparator_1 (.a(A[11:4]), .b(8'h1), .eq(comparator_1_eq));  // open: gt, lt
  and and_1 (and_1_out, RWB, sel);
  and and_2 (sel, comparator_1_eq, IO_EN);
  and and_3 (and_3_out, ~RWB, sel);  // AND_Gate
  and and_4 (and_4_out, Di[7], and_3_out);
  or or_1 (TRM_RST, and_4_out, RST);
  and and_5 (TRM_CLK, and_3_out, CLK);

  assign TRM_ASCII = Di[6:0];

  // Notes on the sheet:
  //   Do: pull=down
endmodule

module PIC2 (
  input  IR7,
  input  IR6,
  input  IR5,
  input  IR4,
  input  [15:0] A,
  input  IO_EN,
  input  RST,
  input  IR3,
  input  RWB,
  input  IR2,
  input  IR1,
  input  IR0,
  output IRQ,
  output [7:0] Do
);

  wire comparator_1_eq, decoder_1_out0, decoder_1_out1, decoder_1_out2, decoder_1_out3, decoder_1_out4,
       decoder_1_out5, decoder_1_out6, decoder_1_out7, IR0_t, IR1_t, IR2_t, IR3_t, IR4_t, IR5_t, IR6_t,
       IR7_t, or_1_out, or_2_out, or_3_out, or_4_out, or_5_out, or_6_out, or_7_out, or_8_out,
       priority_encoder_1_gs, rd, sel, wr;
  wire [2:0] isr_t, priority_encoder_1_out;
  wire [7:0] IMR, ISR;

  D_Flip_Flop d_ff_1 (.D(1'b1), .clk(IR7), .Q(IR7_t), .reset(or_1_out));  // open: Qn, preset
  or or_1 (or_1_out, RST, decoder_1_out7);
  D_Flip_Flop d_ff_2 (.D(1'b1), .clk(IR6), .Q(IR6_t), .reset(or_2_out));  // open: Qn, preset
  or or_2 (or_2_out, RST, decoder_1_out6);
  D_Flip_Flop d_ff_3 (.D(1'b1), .clk(IR5), .Q(IR5_t), .reset(or_3_out));  // open: Qn, preset
  or or_3 (or_3_out, RST, decoder_1_out5);
  D_Flip_Flop d_ff_4 (.D(1'b1), .clk(IR4), .Q(IR4_t), .reset(or_4_out));  // open: Qn, preset
  or or_4 (or_4_out, RST, decoder_1_out4);
  D_Flip_Flop d_ff_5 (.D(1'b1), .clk(IR3), .Q(IR3_t), .reset(or_5_out));  // open: Qn, preset
  or or_5 (or_5_out, RST, decoder_1_out3);
  D_Flip_Flop d_ff_6 (.D(1'b1), .clk(IR2), .Q(IR2_t), .reset(or_6_out));  // open: Qn, preset
  or or_6 (or_6_out, RST, decoder_1_out2);
  D_Flip_Flop d_ff_7 (.D(1'b1), .clk(IR1), .Q(IR1_t), .reset(or_7_out));  // open: Qn, preset
  or or_7 (or_7_out, RST, decoder_1_out1);
  D_Flip_Flop d_ff_8 (.D(1'b1), .clk(IR0), .Q(IR0_t), .reset(or_8_out));  // open: Qn, preset
  or or_8 (or_8_out, RST, decoder_1_out0);
  Decoder #(.select(3)) decoder_1 (
    .out0(decoder_1_out0), .out1(decoder_1_out1), .out2(decoder_1_out2), .out3(decoder_1_out3),
    .out4(decoder_1_out4), .out5(decoder_1_out5), .out6(decoder_1_out6), .out7(decoder_1_out7));  // open: sel, en
  assign isr_t = priority_encoder_1_gs ? ~priority_encoder_1_out : 3'bz;  // Controlled_Inverter controlled_inverter_1
  Priority_Encoder priority_encoder_1 (
    .in0(IR7_t), .in1(IR6_t), .in2(IR5_t), .in3(IR4_t), .in4(IR3_t), .in5(IR2_t), .in6(IR1_t), .in7(IR0_t),
    .out(priority_encoder_1_out), .gs(priority_encoder_1_gs));  // open: en_in, en_out
  Comparator #(.mode("unsigned")) comparator_1 (.a(A[11:4]), .b({8{1'b0}}), .eq(comparator_1_eq));  // open: gt, lt
  and and_1 (rd, RWB, sel);
  and and_2 (wr, sel, ~RWB);  // AND_Gate
  Decoder #(.enable("false"), .select(3)) decoder_2 (
    .out0(ISR[0]), .out1(ISR[1]), .out2(ISR[2]), .out3(ISR[3]), .out4(ISR[4]), .out5(ISR[5]), .out6(ISR[6]),
    .out7(ISR[7]), .sel(isr_t));
  and and_3 (sel, comparator_1_eq, IO_EN);
  not not_1 (IRQ, priority_encoder_1_gs);
  Multiplexer #(.disabled("Z"), .enable("true"), .select(2), .width(8)) multiplexer_1 (
    .out(Do), .en(rd));  // open: in0, in1, in2, in3, sel
  Register #(.trigger("high")) u_IMR (.Q(IMR), .clr(RST));  // open: D, en, clk

  // Other names for the same wires on the sheet: IRR[7:0] = {IR7_t, IR6_t, IR5_t, IR4_t, IR3_t, IR2_t, IR1_t, IR0_t}

  // Notes on the sheet:
  //   IR6: pull=down
  //   IR5: pull=down
  //   IR4: pull=down
  //   IR3: pull=down
  //   IR7: pull=down
  //   IR2: pull=down
  //   IR1: pull=down
  //   IR0: pull=down
endmodule
